// Logisim project And.circ as structural Verilog
module logic_gates (
  input  in_1,
  input  in_2,
  input  in_3,
  input  in_4,
  input  in_5,
  input  in_6,
  input  in_7,
  input  in_8,
  input  in_9,
  input  in_10,
  input  in_11,
  input  in_12,
  input  in_13,
  input  in_14,
  input  in_15,
  input  in_16,
  output out_17,
  output out_18,
  output out_19,
  output out_20,
  output out_21,
  output out_22,
  output out_23,
  output out_24
);

  and and_1 (out_17, in_2, in_1);
  and and_2 (out_18, in_4, in_3);
  and and_3 (out_19, in_6, in_5);
  and and_4 (out_20, in_8, in_7);
  or or_1 (out_21, in_10, in_9);
  or or_2 (out_22, in_12, in_11);
  or or_3 (out_23, in_14, in_13);
  or or_4 (out_24, in_16, in_15);
endmodule

module D_Latch (
  input  in_1,
  input  in_2,
  output out_3,
  output out_4
);

  wire and_1_out, and_2_out, not_1_out;

  not not_1 (not_1_out, in_1);
  and and_1 (and_1_out, in_1, in_2);
  and and_2 (and_2_out, in_2, not_1_out);
  nor nor_1 (out_3, and_1_out, out_4);
  nor nor_2 (out_4, out_3, and_2_out);
endmodule

module D_Flip_Flop (
  input  WE,
  input  \input ,
  input  clock,
  input  AscSet0,
  output \output 
);

  wire d_latch_2_out_3, multiplexer_1_out, not_1_out;

  Pull_Resistor pull_resistor_1 (.node(AscSet0));
  Pull_Resistor #(.pull(1)) pull_resistor_2 (.node(AscSet0));
  Multiplexer #(.enable("false")) multiplexer_1 (.in0(\output ), .in1(\input ), .out(multiplexer_1_out), .sel(AscSet0));
  not not_1 (not_1_out, clock);
  D_Latch d_latch_1 (.in_1(d_latch_2_out_3), .out_3(\output ), .out_4(AscSet0), .in_2(clock));
  D_Latch d_latch_2 (.in_1(multiplexer_1_out), .out_3(d_latch_2_out_3), .out_4(AscSet0), .in_2(not_1_out));

  assign WE = AscSet0;
endmodule

module _18_bit_XOR (
  input  [17:0] input_1,
  input  [17:0] input_2,
  output [17:0] out_3
);

  nor nor_1 (out_3[9], input_1[9], input_2[9]);
  nor nor_2 (out_3[10], input_1[10], input_2[10]);
  nor nor_3 (out_3[11], input_1[11], input_2[11]);
  nor nor_4 (out_3[12], input_1[12], input_2[12]);
  nor nor_5 (out_3[13], input_1[13], input_2[13]);
  nor nor_6 (out_3[14], input_1[14], input_2[14]);
  nor nor_7 (out_3[15], input_1[15], input_2[15]);
  nor nor_8 (out_3[16], input_1[16], input_2[16]);
  nor nor_9 (out_3[17], input_1[17], input_2[17]);
  nor nor_10 (out_3[0], input_1[0], input_2[0]);
  nor nor_11 (out_3[1], input_1[1], input_2[1]);
  nor nor_12 (out_3[2], input_1[2], input_2[2]);
  nor nor_13 (out_3[3], input_1[3], input_2[3]);
  nor nor_14 (out_3[4], input_1[4], input_2[4]);
  nor nor_15 (out_3[5], input_1[5], input_2[5]);
  nor nor_16 (out_3[6], input_1[6], input_2[6]);
  nor nor_17 (out_3[7], input_1[7], input_2[7]);
  nor nor_18 (out_3[8], input_1[8], input_2[8]);
endmodule

module _18_bit_AND (
  input  [17:0] input_1,
  input  [17:0] input_2,
  output [17:0] out_3
);

  and and_1 (out_3[9], input_1[9], input_2[9]);
  and and_2 (out_3[10], input_1[10], input_2[10]);
  and and_3 (out_3[11], input_1[11], input_2[11]);
  and and_4 (out_3[12], input_1[12], input_2[12]);
  and and_5 (out_3[13], input_1[13], input_2[13]);
  and and_6 (out_3[14], input_1[14], input_2[14]);
  and and_7 (out_3[15], input_1[15], input_2[15]);
  and and_8 (out_3[16], input_1[16], input_2[16]);
  and and_9 (out_3[17], input_1[17], input_2[17]);
  and and_10 (out_3[0], input_1[0], input_2[0]);
  and and_11 (out_3[1], input_1[1], input_2[1]);
  and and_12 (out_3[2], input_1[2], input_2[2]);
  and and_13 (out_3[3], input_1[3], input_2[3]);
  and and_14 (out_3[4], input_1[4], input_2[4]);
  and and_15 (out_3[5], input_1[5], input_2[5]);
  and and_16 (out_3[6], input_1[6], input_2[6]);
  and and_17 (out_3[7], input_1[7], input_2[7]);
  and and_18 (out_3[8], input_1[8], input_2[8]);
endmodule

module _18_bit_NAND (
  input  [17:0] input_1,
  input  [17:0] input_2,
  output [17:0] out_3
);

  nand nand_1 (out_3[9], input_1[9], input_2[9]);
  nand nand_2 (out_3[10], input_1[10], input_2[10]);
  nand nand_3 (out_3[11], input_1[11], input_2[11]);
  nand nand_4 (out_3[12], input_1[12], input_2[12]);
  nand nand_5 (out_3[13], input_1[13], input_2[13]);
  nand nand_6 (out_3[14], input_1[14], input_2[14]);
  nand nand_7 (out_3[15], input_1[15], input_2[15]);
  nand nand_8 (out_3[16], input_1[16], input_2[16]);
  nand nand_9 (out_3[17], input_1[17], input_2[17]);
  nand nand_10 (out_3[0], input_1[0], input_2[0]);
  nand nand_11 (out_3[1], input_1[1], input_2[1]);
  nand nand_12 (out_3[2], input_1[2], input_2[2]);
  nand nand_13 (out_3[3], input_1[3], input_2[3]);
  // NAND_Gate nand_14 has open pins: in0=input_1[4], in1=input_2[4], out=open
  nand nand_15 (out_3[5], input_1[5], input_2[5]);
  nand nand_16 (out_3[6], input_1[6], input_2[6]);
  nand nand_17 (out_3[7], input_1[7], input_2[7]);
  nand nand_18 (out_3[8], input_1[8], input_2[8]);
endmodule

module _18_bit_OR (
  input  [17:0] input_1,
  input  [17:0] input_2,
  output [17:0] out_3
);

  or or_1 (out_3[9], input_1[9], input_2[9]);
  or or_2 (out_3[10], input_1[10], input_2[10]);
  or or_3 (out_3[11], input_1[11], input_2[11]);
  or or_4 (out_3[12], input_1[12], input_2[12]);
  or or_5 (out_3[13], input_1[13], input_2[13]);
  or or_6 (out_3[14], input_1[14], input_2[14]);
  or or_7 (out_3[15], input_1[15], input_2[15]);
  or or_8 (out_3[16], input_1[16], input_2[16]);
  or or_9 (out_3[17], input_1[17], input_2[17]);
  or or_10 (out_3[0], input_1[0], input_2[0]);
  or or_11 (out_3[1], input_1[1], input_2[1]);
  or or_12 (out_3[2], input_1[2], input_2[2]);
  or or_13 (out_3[3], input_1[3], input_2[3]);
  or or_14 (out_3[4], input_1[4], input_2[4]);
  or or_15 (out_3[5], input_1[5], input_2[5]);
  or or_16 (out_3[6], input_1[6], input_2[6]);
  or or_17 (out_3[7], input_1[7], input_2[7]);
  or or_18 (out_3[8], input_1[8], input_2[8]);
endmodule
